// Logisim project ME Serial V2.circ as structural Verilog: 1 circuit, main circuit main
module main (
  input  Bit_Ready,
  input  Bit_Ready_2,
  input  Byte_Ready,
  input  Byte_Ready_2,
  input  Error,
  input  Error_2,
  input  Load,
  input  Load_2,
  input  [7:0] Data,
  input  [7:0] Data_2,
  output [7:0] Data_3,
  output [7:0] Data_4
);

  wire not_1_out, not_2_out, or_1_out, or_2_out, shift_register_1_out, shift_register_2_out;

  not not_1 (not_1_out, Load);
  Shift_Register shift_register_1 (
    .shift(not_1_out), .in(shift_register_2_out), .clk(or_2_out), .out(shift_register_1_out), .load(Load),
    .clr(Error_2), .d0(Data[7]), .q0(Data_3[7]), .d1(Data[6]), .q1(Data_3[6]), .d2(Data[5]), .q2(Data_3[5]),
    .d3(Data[4]), .q3(Data_3[4]), .d4(Data[3]), .q4(Data_3[3]), .d5(Data[2]), .q5(Data_3[2]), .d6(Data[1]),
    .q6(Data_3[1]), .d7(Data[0]), .q7(Data_3[0]));
  or or_1 (or_1_out, Bit_Ready, Bit_Ready_2, Load_2);
  or or_2 (or_2_out, Bit_Ready_2, Bit_Ready, Load);
  not not_2 (not_2_out, Load_2);
  Shift_Register shift_register_2 (
    .shift(not_2_out), .in(shift_register_1_out), .clk(or_1_out), .out(shift_register_2_out), .load(Load_2),
    .clr(Error), .d0(Data_2[7]), .q0(Data_4[7]), .d1(Data_2[6]), .q1(Data_4[6]), .d2(Data_2[5]),
    .q2(Data_4[5]), .d3(Data_2[4]), .q3(Data_4[4]), .d4(Data_2[3]), .q4(Data_4[3]), .d5(Data_2[2]),
    .q5(Data_4[2]), .d6(Data_2[1]), .q6(Data_4[1]), .d7(Data_2[0]), .q7(Data_4[0]));

  // Notes on the sheet:
  //   Computer
  //   Peripheral
endmodule
