// Logisim project cpu.circ as structural Verilog: 3 circuits, main circuit main
module main (
);

  wire alu_1_c, alu_1_z, clock_1_out, ins_dec_1_add, ins_dec_1_out, ins_dec_1_res, ins_dec_1_sub, or_1_out,
       pull_resistor_2_node, pull_resistor_5_node, res_out, undriven, undriven_3;
  wire [3:0] bit_extender_1_out;
  wire [7:0] pull_resistor_1_node, pull_resistor_3_node, pull_resistor_4_node, ram_1_data, register_1_q,
       register_4_q, register_5_q, undriven_2, undriven_4;
  wire [15:0] rom_1_data;

  Button res (.out(res_out));
  Clock clock_1 (.out(clock_1_out));
  Button _0 ();  // open: out
  Button _4 ();  // open: out
  Button _8 ();  // open: out
  Button C ();  // open: out
  or or_1 (or_1_out, res_out, ins_dec_1_res);
  Pull_Resistor pull_resistor_1 (.node(pull_resistor_1_node));
  Button _1 ();  // open: out
  Button _5 ();  // open: out
  Button _9 ();  // open: out
  Button D ();  // open: out
  Pull_Resistor pull_resistor_2 (.node(pull_resistor_2_node));
  Button _2 ();  // open: out
  Button _6 ();  // open: out
  Button A ();  // open: out
  Button E ();  // open: out
  Pull_Resistor pull_resistor_3 (.node(pull_resistor_3_node));
  Pull_Resistor pull_resistor_4 (.node(pull_resistor_4_node));
  Pull_Resistor #(.pull(1)) pull_resistor_5 (.node(pull_resistor_5_node));
  ROM #(.dataWidth(16)) rom_1 (.addr(pull_resistor_1_node), .data(rom_1_data));  // open: sel
  Button _3 ();  // open: out
  Button _7 ();  // open: out
  Button B ();  // open: out
  Button F ();  // open: out
  Bit_Extender #(.out_width(4)) bit_extender_1 (.in(rom_1_data[15:8]), .out(bit_extender_1_out));
  alu alu_1 (
    .add(ins_dec_1_add), .sub(ins_dec_1_sub), .a(register_5_q), .b(register_4_q), .z(alu_1_z), .c(alu_1_c));  // open: r
  ins_dec ins_dec_1 (
    .in_1(bit_extender_1_out), .add(ins_dec_1_add), .sub(ins_dec_1_sub), .out(ins_dec_1_out),
    .res(ins_dec_1_res));  // open: lda, ldb, sta, stb, in, jmp, jic, jinc, jiz, jinz
  Register register_1 (.D(ram_1_data), .en(ins_dec_1_out), .Q(register_1_q), .clk(clock_1_out), .clr(or_1_out));
  RAM #(.bus("separate")) ram_1 (
    .addr(pull_resistor_4_node), .din(pull_resistor_3_node), .data(ram_1_data), .str(pull_resistor_2_node),
    .clk(clock_1_out), .ld(pull_resistor_5_node), .clr(or_1_out));  // open: sel
  Register #(.width(1)) register_2 (.D(alu_1_z), .clk(clock_1_out), .clr(or_1_out));  // open: en, Q
  Register #(.width(1)) register_3 (.D(alu_1_c), .clk(clock_1_out), .clr(or_1_out));  // open: en, Q
  Hex_Digit_Display hex_digit_display_1 (.value(register_1_q[7:4]));  // open: dp
  Register register_4 (.D(undriven_4), .en(undriven_3), .Q(register_4_q), .clk(clock_1_out), .clr(or_1_out));
  Register register_5 (.D(undriven_2), .en(undriven), .Q(register_5_q), .clk(clock_1_out), .clr(or_1_out));
  Hex_Digit_Display hex_digit_display_2 (.value(register_1_q[3:0]));  // open: dp
endmodule

module ins_dec (
  input  [3:0] in_1,
  output lda,
  output ldb,
  output sta,
  output stb,
  output add,
  output sub,
  output in,
  output out,
  output jmp,
  output jic,
  output jinc,
  output jiz,
  output jinz,
  output res
);

  Comparator #(.width(4)) comparator_1 (.a(4'b0000), .b(in_1), .eq(lda));  // open: gt, lt
  Comparator #(.width(4)) comparator_2 (.a(4'b0001), .b(in_1), .eq(ldb));  // open: gt, lt
  Comparator #(.width(4)) comparator_3 (.a(4'b0010), .b(in_1), .eq(sta));  // open: gt, lt
  Comparator #(.width(4)) comparator_4 (.a(4'b0011), .b(in_1), .eq(stb));  // open: gt, lt
  Comparator #(.width(4)) comparator_5 (.a(4'b0100), .b(in_1), .eq(add));  // open: gt, lt
  Comparator #(.width(4)) comparator_6 (.a(4'b0101), .b(in_1), .eq(sub));  // open: gt, lt
  Comparator #(.width(4)) comparator_7 (.a(4'b0110), .b(in_1), .eq(in));  // open: gt, lt
  Comparator #(.width(4)) comparator_8 (.a(4'b0111), .b(in_1), .eq(out));  // open: gt, lt
  Comparator #(.width(4)) comparator_9 (.a(4'b1000), .b(in_1), .eq(jmp));  // open: gt, lt
  Comparator #(.width(4)) comparator_10 (.a(4'b1001), .b(in_1), .eq(jic));  // open: gt, lt
  Comparator #(.width(4)) comparator_11 (.a(4'b1010), .b(in_1), .eq(jinc));  // open: gt, lt
  Comparator #(.width(4)) comparator_12 (.a(4'b1011), .b(in_1), .eq(jiz));  // open: gt, lt
  Comparator #(.width(4)) comparator_13 (.a(4'b1100), .b(in_1), .eq(jinz));  // open: gt, lt
  Comparator #(.width(4)) comparator_14 (.a(4'b1101), .b(in_1), .eq(res));  // open: gt, lt
endmodule

module alu (
  input  add,
  input  sub,
  input  [7:0] a,
  input  [7:0] b,
  output [7:0] r,
  output z,
  output c
);

  wire adder_1_cout, or_1_out, subtractor_1_bout;
  wire [7:0] adder_1_out, subtractor_1_out;

  Adder adder_1 (.a(a), .b(b), .out(adder_1_out), .cout(adder_1_cout));  // open: cin
  Subtractor subtractor_1 (.a(a), .b(b), .out(subtractor_1_out), .bout(subtractor_1_bout));  // open: bin
  or or_1 (or_1_out, add, sub);
  Multiplexer #(.width(8)) multiplexer_1 (.in0(adder_1_out), .in1(subtractor_1_out), .out(r), .sel(sub), .en(or_1_out));
  Comparator comparator_1 (.a({8{1'b0}}), .b(r), .eq(z));  // open: gt, lt
  Multiplexer multiplexer_2 (.in0(adder_1_cout), .in1(subtractor_1_bout), .out(c), .sel(sub), .en(or_1_out));
endmodule
