// Logisim project te.circ as structural Verilog: 1 circuit, main circuit main
module main (
  input  in_1
);

  wire and_1_out, and_2_out, button_1_out, clock_1_out, keyboard_1_avail, not_1_out, or_1_out, or_2_out,
       or_3_out;
  wire [6:0] keyboard_1_data, multiplexer_1_out, ram_1_data;
  wire [23:0] counter_1_q;

  Keyboard keyboard_1 (.clk(and_1_out), .avail(keyboard_1_avail), .data(keyboard_1_data));  // open: re, clr
  Clock clock_1 (.out(clock_1_out));
  Button button_1 (.out(button_1_out));
  and and_1 (and_1_out, clock_1_out, ~button_1_out);  // AND_Gate
  Counter #(.width(24), .max('hffffff)) counter_1 (
    .count(or_1_out), .Q(counter_1_q), .clk(and_1_out), .clr(or_2_out));  // open: load, D, carry
  or or_1 (or_1_out, or_3_out, keyboard_1_avail);
  or or_2 (or_2_out, button_1_out, and_2_out);
  and and_2 (and_2_out, ~or_3_out, in_1);  // AND_Gate
  not not_1 (not_1_out, keyboard_1_avail);
  RAM #(.addrWidth(24), .dataWidth(7), .bus("separate")) ram_1 (
    .addr(counter_1_q), .din(keyboard_1_data), .data(ram_1_data), .str(keyboard_1_avail), .clk(and_1_out),
    .ld(not_1_out));  // open: sel, clr
  TTY tty_1 (.data(multiplexer_1_out), .clk(and_1_out), .clr(or_2_out));  // open: we
  Multiplexer #(.width(7), .disabled(0), .enable("false")) multiplexer_1 (
    .in0(ram_1_data), .in1(keyboard_1_data), .out(multiplexer_1_out), .sel(keyboard_1_avail));
  or or_3 (or_3_out, multiplexer_1_out[0], multiplexer_1_out[1], multiplexer_1_out[2], multiplexer_1_out[3], multiplexer_1_out[4], multiplexer_1_out[5], multiplexer_1_out[6]);
  DotMatrix #(.matrixcols(12), .matrixrows(1)) dotmatrix_1 (
    .col0(multiplexer_1_out[6]), .col1(multiplexer_1_out[5]), .col2(multiplexer_1_out[4]),
    .col3(multiplexer_1_out[3]), .col4(multiplexer_1_out[2]), .col5(multiplexer_1_out[1]),
    .col6(multiplexer_1_out[0]), .col7(and_1_out), .col8(in_1), .col9(keyboard_1_avail), .col10(not_1_out),
    .col11(or_2_out));
endmodule
